# Fritzing sketch Tesseract (saved by Fritzing 0.8.7b)
breadboards: 1

parts:
  L293D_Motor_Driver = L293D [package=THT]
  Raspberry_Pi_B_rev1 = Raspberry Pi B rev1
  V1 = DC Power [voltage=5]
  DC_Motor = DC Motor
  J1 = Basic Servo
  J2 = Basic Servo

nets (from the schematic view):
  GND: L293D_Motor_Driver.0V, Raspberry_Pi_B_rev1.GND, V1.V-, DC_Motor.pin_2, J1.gnd, J2.gnd
  VCC: L293D_Motor_Driver.+Vmotor, L293D_Motor_Driver.Enable_2, Raspberry_Pi_B_rev1.5V, V1.V+, J1.vcc, J2.vcc
  N1: L293D_Motor_Driver.Out_4_(_Controlled_by_Enable_2_), DC_Motor.pin_1
  N2: L293D_Motor_Driver.In_4, Raspberry_Pi_B_rev1.GPIO_23
  N3: Raspberry_Pi_B_rev1.GPIO_17, J2.pulse
  N4: Raspberry_Pi_B_rev1.GPIO_18, J1.pulse
